# Fritzing sketch circuit-sketch (saved by Fritzing 0.9.10b)
breadboards: 1

parts:
  Part3 = Arduino Leonardo (Rev3b)
  A3 = L298N DC motor driver
  Q4 = NPN-Transistor [package="TO92 [THT]"]
  Q6 = NPN-Transistor [package="TO92 [THT]"]
  Q7 = NPN-Transistor [package="TO92 [THT]"]
  Q8 = NPN-Transistor [package="TO92 [THT]"]
  Q9 = NPN-Transistor [package="TO92 [THT]"]
  M3 = DC Motor [voltage_(max)=6V voltage_(min)=3V]
  Rotary1 = Rotary Encoder [package=THT]
  BAT3 = BC9VPC [package=bc9vpc]
  LED3 = 2-digit 7-segment [package=THT-longpads]
  Q10 = NPN-Transistor [package="TO92 [THT]"]
  Q11 = NPN-Transistor [package="TO92 [THT]"]
  R1 = Resistor [tolerance=±5% power=0.25 resistance=220 package=THT]
  R2 = Resistor [tolerance=±5% power=0.25 resistance=220 package=THT]

nets:
  N1: Part3.D2/SDA, Q9.B
  N2: Part3.D3_PWM/SCL, Q6.B
  N3: Part3.D4/A6, Q11.B
  N4: Part3.D5_PWM, Q10.B
  N5: Part3.D6_PWM/A7, Q8.B
  N6: Part3.D7, Q7.B
  N7: Part3.5V, Rotary1.SwitchPinE
  N8: Part3.GND, Q4.E, Q6.E, Q7.E, Q8.E, Q9.E, Rotary1.SwitchrPinD, Q10.E, Q11.E
  N9: Part3.A0, Rotary1.EncoderPinA
  N10: Part3.A1, Rotary1.EncoderPinC
  N11: Part3.A2, Rotary1.EncoderPinB
  N12: Part3.D8/A8, Q4.B
  N13: Part3.D9_PWM/A9, R2.Pin_1
  N14: Part3.D10_PWM/A10, R1.Pin_1
  N15: Part3.D11_PWM, A3.IN2
  N16: Part3.D12/A11, A3.IN1
  N17: Part3.D13_PWM, A3.ENA
  N18: A3.OUT1, M3.pin_2
  N19: A3.OUT2, M3.pin_1
  N20: A3.12V, BAT3.V+
  N21: A3.GND, BAT3.V-
  N22: Q4.C, LED3.G
  N23: Q6.C, LED3.B
  N24: Q7.C, LED3.F
  N25: Q8.C, LED3.E
  N26: Q9.C, LED3.A
  N27: LED3.DIG1, R1.Pin_0
  N28: LED3.D, Q10.C
  N29: LED3.DIG2, R2.Pin_0

custom parts:
  L298N DC motor driver: This L298N Motor Driver Module is a high power motor driver module for driving DC and Stepper Motors. This module consists of an L298 motor driver IC and a 78M05 5V regulator.
  Rotary Encoder: Rotary Encoder from ALPSec11e with switch. This version has an alternate (which has been used in boards) pcb footprint from @opera_night in the forums. It is probably the best one to start from to see if you part matches.
  2-digit 7-segment: Fork from generic 7-segment-display, but for the CL4021BH (cathode)
