# Fritzing sketch new-circuit-sketch (saved by Fritzing 0.9.10b)
breadboards: 1

parts:
  Part3 = Arduino Leonardo (Rev3b)
  A3 = L298N DC motor driver
  M3 = DC Motor [voltage_(max)=6V voltage_(min)=3V]
  Rotary1 = Rotary Encoder [package=THT]
  BAT3 = BC9VPC [package=bc9vpc]
  LED3 = 2-digit 7-segment [package=THT-longpads]
  R1 = Resistor [tolerance=±5% power=0.25 resistance=220 package=THT]
  R2 = Resistor [tolerance=±5% power=0.25 resistance=220 package=THT]

nets:
  N1: Part3.D2/SDA, LED3.A
  N2: Part3.D3_PWM/SCL, LED3.B
  N3: Part3.D4/A6, LED3.C
  N4: Part3.D5_PWM, LED3.D
  N5: Part3.D6_PWM/A7, LED3.E
  N6: Part3.D7, LED3.F
  N7: Part3.5V, Rotary1.SwitchPinE
  N8: Part3.GND, Rotary1.SwitchrPinD
  N9: Part3.A0, Rotary1.EncoderPinA
  N10: Part3.A1, Rotary1.EncoderPinC
  N11: Part3.D8/A8, LED3.G
  N12: Part3.D9_PWM/A9, R2.Pin_1
  N13: Part3.D10_PWM/A10, R1.Pin_1
  N14: Part3.D11_PWM, A3.IN2
  N15: Part3.D12/A11, A3.IN1
  N16: Part3.D13_PWM, A3.ENA
  N17: A3.OUT1, M3.pin_2
  N18: A3.OUT2, M3.pin_1
  N19: A3.12V, BAT3.V+
  N20: A3.GND, BAT3.V-
  N21: LED3.DIG1, R1.Pin_0
  N22: LED3.DIG2, R2.Pin_0

custom parts:
  L298N DC motor driver: This L298N Motor Driver Module is a high power motor driver module for driving DC and Stepper Motors. This module consists of an L298 motor driver IC and a 78M05 5V regulator.
  Rotary Encoder: Rotary Encoder from ALPSec11e with switch. This version has an alternate (which has been used in boards) pcb footprint from @opera_night in the forums. It is probably the best one to start from to see if you part matches.
  2-digit 7-segment: Fork from generic 7-segment-display, but for the CL4021BH (cathode)
